// Logisim project DDCA FINAL.circ as structural Verilog: 1 circuit, main circuit main
module main (
  input  DARKNESS,
  input  MOTION,
  output out_3
);

  wire and_1_out, and_2_out, not_1_out;

  not not_1 (not_1_out, DARKNESS);
  and and_1 (and_1_out, not_1_out, MOTION);
  and and_2 (and_2_out, DARKNESS, MOTION);
  or or_1 (out_3, and_1_out, and_2_out);

  // Notes on the sheet:
  //   D  M   Y
  //    0  0  0
  //    0  1  0
  //    1  0  0
  //   1  1  1
endmodule
